// Logisim project 16-bit_FA.circ as structural Verilog: 4 circuits, main circuit main
module main (
  input  A,
  input  B,
  output S,
  output C
);

  xor xor_1 (S, A, B);
  and and_1 (C, A, B);
endmodule

module FA (
  input  X,
  input  Y,
  input  C,
  output S,
  output C_2
);

  wire main_1_c, main_1_s, main_2_c;

  main main_1 (.A(X), .B(Y), .S(main_1_s), .C(main_1_c));
  main main_2 (.A(main_1_s), .B(C), .S(S), .C(main_2_c));
  or or_1 (C_2, main_2_c, main_1_c);
endmodule

module _4_BIT_FA (
  input  C,
  input  [3:0] B,
  input  [3:0] A,
  output [3:0] S,
  output COUT
);

  wire fa_1_c_2, fa_2_c_2, fa_3_c_2;

  FA fa_1 (.X(A[0]), .Y(B[0]), .C(C), .S(S[0]), .C_2(fa_1_c_2));
  FA fa_2 (.X(A[1]), .Y(B[1]), .C(fa_1_c_2), .S(S[1]), .C_2(fa_2_c_2));
  FA fa_3 (.X(A[2]), .Y(B[2]), .C(fa_2_c_2), .S(S[2]), .C_2(fa_3_c_2));
  FA fa_4 (.X(A[3]), .Y(B[3]), .C(fa_3_c_2), .S(S[3]), .C_2(COUT));
endmodule

module _16BIT (
  input  C,
  input  [15:0] A,
  input  [15:0] B,
  output COUT
);

  wire n4_bit_fa_1_cout, n4_bit_fa_2_cout, n4_bit_fa_3_cout;
  wire [3:0] n4_bit_fa_1_s, n4_bit_fa_2_s, n4_bit_fa_3_s, n4_bit_fa_4_s;

  _4_BIT_FA u_4_bit_fa_1 (.C(C), .B(B[3:0]), .A(A[3:0]), .S(n4_bit_fa_1_s), .COUT(n4_bit_fa_1_cout));
  _4_BIT_FA u_4_bit_fa_2 (.C(n4_bit_fa_1_cout), .B(B[7:4]), .A(A[7:4]), .S(n4_bit_fa_2_s), .COUT(n4_bit_fa_2_cout));
  _4_BIT_FA u_4_bit_fa_3 (.C(n4_bit_fa_2_cout), .B(B[11:8]), .A(A[11:8]), .S(n4_bit_fa_3_s), .COUT(n4_bit_fa_3_cout));
  _4_BIT_FA u_4_bit_fa_4 (.C(n4_bit_fa_3_cout), .B(B[15:12]), .A(A[15:12]), .S(n4_bit_fa_4_s), .COUT(COUT));
  Hex_Digit_Display hex_digit_display_1 (.value(n4_bit_fa_4_s));  // open: dp
  Hex_Digit_Display hex_digit_display_2 (.value(n4_bit_fa_3_s));  // open: dp
  Hex_Digit_Display hex_digit_display_3 (.value(n4_bit_fa_2_s));  // open: dp
  Hex_Digit_Display hex_digit_display_4 (.value(n4_bit_fa_1_s));  // open: dp
endmodule
